# Fritzing sketch ContadorPulsos (saved by Fritzing 0.9.3b)
breadboards: 1

parts:
  S1 = Round Pushbutton
  LCD1 = LCD screen
  Componente2 = Adafruit I2C+SPI LCD Backpack [part_number="Adafruit #292"]
  R1 = Resistor [tolerance=±5% resistance=220 package="2512 [SMD]"]
  Componente1 = Arduino Uno (Rev3)

nets:
  N1: S1.leg0, R1.Pin_1
  VDD: S1.leg1, LCD1.VDD, LCD1.LED+, Componente2.VCC, Componente1.5V
  GND: LCD1.VSS, LCD1.R/W, Componente2.GND, Componente1.GND
  N2: LCD1.V0, Componente2.CONTRAST
  N3: LCD1.RS, Componente2.RS
  N4: LCD1.E, Componente2.E
  N5: LCD1.DB0, Componente2.DB0
  N6: LCD1.DB1, Componente2.DB1
  N7: LCD1.DB2, Componente2.DB2
  N8: LCD1.DB3, Componente2.DB3
  N9: LCD1.DB4, Componente2.DB4
  N10: LCD1.DB5, Componente2.DB5
  N11: LCD1.DB6, Componente2.DB6
  N12: LCD1.DB7, Componente2.DB7
  N13: LCD1.LED-, Componente2.LEDK
  N14: Componente2.CLOCK, Componente1.A5/SCL
  N15: Componente2.DATA, Componente1.A4/SDA
  N16: R1.Pin_0, Componente1.D2

custom parts:
  Adafruit I2C+SPI LCD Backpack: LCD backpacks reduce the number of pins needed to connect to an LCD. LCDs are a fun and easy way to have your microcontroller project talk back to you. Character LCDs are common, and easy to get, available in tons of colors and sizes. We've written tutorials on using character LCDs with an Arduino (or similar microcontroller) but find that the number of pins necessary to control the LCD can be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
